# Fritzing sketch simpleremindersketch (saved by Fritzing 0.7.7b)
breadboards: 1

parts:
  Arduino1 = Arduino
  LED1 = RGB LED (com. cathode, rbg) [package="5 mm [THT]"]  # not connected
  R1 = Resistor [tolerance=±5% resistance=330 package="0805 [SMD]"]
  R2 = Resistor [tolerance=±5% resistance=330 package="0805 [SMD]"]
  R3 = Resistor [tolerance=±5% resistance=330 package="0805 [SMD]"]

nets:
  N1: Arduino1.D11, R3.Pin_1
  N2: Arduino1.D10, R2.Pin_1
  N3: Arduino1.D9, R1.Pin_1
